// Logisim project brachocpu.circ as structural Verilog
module cpu (
);

  wire MAINCLOCK_out;
  wire [15:0] alu_1_acc, registerbank_1_balu, registerbank_1_calu;

  Clock MAINCLOCK (.out(MAINCLOCK_out));
  ALU alu_1 (
    .B(registerbank_1_balu), .C(registerbank_1_calu), .ACC(alu_1_acc));  // open: Cin, op, ZERO, NEGATIVE, OVERFLOW
  RegisterBank registerbank_1 (
    .ACC(alu_1_acc), .CLK(MAINCLOCK_out), .BALU(registerbank_1_balu), .CALU(registerbank_1_calu));  // open: AddressBus, DataBus, ControlBus, IRout
  RAM #(.addrWidth(12), .dataWidth(16)) ram_1 ();  // open: addr, we, oe, clk, din, dout
endmodule

module ALU (
  input  Cin,
  input  [15:0] B,
  input  [15:0] C,
  input  [3:0] op,
  output [15:0] ACC,
  output ZERO,
  output NEGATIVE,
  output OVERFLOW
);

  wire adder_1_cout, comparator_1_eq, not_2_out, or_2_out, or_3_out;
  wire [15:0] adder_1_out, and_1_out, divider_1_out, multiplier_1_cout, multiplier_1_out, not_1_out,
       or_1_out, shifter_1_out, shifter_2_out, subtractor_1_out, xor_1_out;

  assign not_1_out = ~B;  // NOT_Gate not_1, 16 bits wide
  assign and_1_out = B & C;  // AND_Gate and_1, 16 bits wide
  assign or_1_out = B | C;  // OR_Gate or_1, 16 bits wide
  Adder #(.width(16)) adder_1 (.a(B), .b(C), .out(adder_1_out), .cin(Cin), .cout(adder_1_cout));
  Subtractor #(.width(16)) subtractor_1 (.a(B), .b(C), .out(subtractor_1_out));  // open: bin, bout
  Multiplier #(.width(16)) multiplier_1 (
    .a(B), .b(C), .out(multiplier_1_out), .cin({16{1'b0}}), .cout(multiplier_1_cout));
  Divider #(.width(16)) divider_1 (.a(B), .b(C), .out(divider_1_out), .upper({16{1'b0}}));  // open: rem
  assign xor_1_out = B ^ C;  // XOR_Gate xor_1, 16 bits wide
  Shifter #(.width(16)) shifter_1 (.in(B), .\dist (C[3:0]), .out(shifter_1_out));
  Shifter #(.shift("lr"), .width(16)) shifter_2 (.in(B), .\dist (C[3:0]), .out(shifter_2_out));
  Comparator #(.width(16)) comparator_1 (.a(B), .b(C), .eq(comparator_1_eq), .lt(NEGATIVE));  // open: gt
  Multiplexer #(.select(4), .width(16)) multiplexer_1 (
    .in0(adder_1_out), .in1(subtractor_1_out), .in2(multiplier_1_out), .in3(divider_1_out), .in4(not_1_out),
    .in5(and_1_out), .in6(or_1_out), .in7(shifter_1_out), .in8(shifter_2_out), .in9(xor_1_out), .out(ACC),
    .sel(op));  // open: in10, in11, in12, in13, in14, in15
  or or_2 (or_2_out, multiplier_1_cout[0], multiplier_1_cout[1], multiplier_1_cout[2], multiplier_1_cout[3], multiplier_1_cout[4], multiplier_1_cout[5], multiplier_1_cout[6], multiplier_1_cout[7], multiplier_1_cout[8], multiplier_1_cout[9], multiplier_1_cout[10], multiplier_1_cout[11], multiplier_1_cout[12], multiplier_1_cout[13], multiplier_1_cout[14], multiplier_1_cout[15]);
  or or_3 (or_3_out, ACC[0], ACC[1], ACC[2], ACC[3], ACC[4], ACC[5], ACC[6], ACC[7], ACC[8], ACC[9], ACC[10], ACC[11], ACC[12], ACC[13], ACC[14], ACC[15]);
  not not_2 (not_2_out, or_3_out);
  or or_4 (ZERO, not_2_out, comparator_1_eq);
  or or_5 (OVERFLOW, adder_1_cout, or_2_out);
endmodule

module RegisterBank (
  input  [11:0] AddressBus,
  input  [15:0] DataBus,
  input  [16:0] ControlBus,
  input  [15:0] ACC,
  input  CLK,
  output [15:0] BALU,
  output [15:0] CALU,
  output [3:0] IRout
);

  wire [6:0] pull_resistor_1_node;
  wire [11:0] InstructionRegister_q, LinkRegister_q;
  wire [15:0] accumulator_q, bit_extender_1_out, RegisterA_q;

  // Probe on ControlBus[14]
  // Probe on ControlBus[15]
  // Probe on pull_resistor_1_node
  // Probe on ControlBus[13:7]
  Pull_Resistor pull_resistor_1 (.node(pull_resistor_1_node));
  assign pull_resistor_1_node = ControlBus[16] ? {7{1'b1}} : 7'bz;  // Controlled_Buffer controlled_buffer_1
  Register #(.width(12)) LinkRegister (
    .D(AddressBus), .en(pull_resistor_1_node[0]), .clk(CLK), .Q(LinkRegister_q), .clr(ControlBus[13]));
  Register #(.width(16)) RegisterA (
    .D(DataBus), .en(pull_resistor_1_node[6]), .clk(CLK), .Q(RegisterA_q), .clr(ControlBus[11]));
  Register #(.width(16)) RegisterB (
    .D(DataBus), .en(pull_resistor_1_node[5]), .clk(CLK), .Q(BALU), .clr(ControlBus[10]));
  Register #(.width(16)) RegisterC (
    .D(DataBus), .en(pull_resistor_1_node[4]), .clk(CLK), .Q(CALU), .clr(ControlBus[9]));
  Register #(.width(16)) accumulator (
    .D(ACC), .en(pull_resistor_1_node[3]), .clk(CLK), .Q(accumulator_q), .clr(ControlBus[8]));
  Register #(.width(16)) InstructionRegister (
    .D(DataBus), .en(pull_resistor_1_node[2]), .clk(CLK), .Q({IRout, InstructionRegister_q}),
    .clr(ControlBus[7]));
  Programcounter programcounter_1 (
    .DataBus(DataBus), .AdressBus(AddressBus), .PIDATA(ControlBus[14]), .INC(ControlBus[15]),
    .PI(pull_resistor_1_node[1]), .PO(ControlBus[5]), .CLK(CLK), .R(ControlBus[12]));
  Pull_Resistor pull_resistor_2 (.node(ControlBus));
  assign DataBus = ControlBus[1] ? BALU : 16'bz;  // Controlled_Buffer controlled_buffer_2
  assign DataBus = ControlBus[2] ? CALU : 16'bz;  // Controlled_Buffer controlled_buffer_3
  assign DataBus = ControlBus[3] ? accumulator_q : 16'bz;  // Controlled_Buffer controlled_buffer_4
  assign DataBus = ControlBus[4] ? bit_extender_1_out : 16'bz;  // Controlled_Buffer controlled_buffer_5
  assign bit_extender_1_out = {{4{1'b0}}, InstructionRegister_q};  // Bit_Extender bit_extender_1
  // Probe on ControlBus[6:0]
  assign DataBus = ControlBus[0] ? RegisterA_q : 16'bz;  // Controlled_Buffer controlled_buffer_6
  assign AddressBus = ControlBus[6] ? LinkRegister_q : 12'bz;  // Controlled_Buffer controlled_buffer_7
endmodule

module Programcounter (
  input  [15:0] DataBus,
  input  [11:0] AdressBus,
  input  PIDATA,
  input  INC,
  input  PI,
  input  PO,
  input  CLK,
  input  R
);

  wire counter_1_carry, not_1_out, or_1_out;
  wire [11:0] counter_1_q;
  wire [15:0] controlled_buffer_2_out;

  assign AdressBus = PO ? counter_1_q : 12'bz;  // Controlled_Buffer controlled_buffer_1
  or or_1 (or_1_out, counter_1_carry, R);
  assign controlled_buffer_2_out = PIDATA ? DataBus : 16'bz;  // Controlled_Buffer controlled_buffer_2
  assign controlled_buffer_2_out[11:0] = not_1_out ? AdressBus : 12'bz;  // Controlled_Buffer controlled_buffer_3
  not not_1 (not_1_out, PIDATA);
  Counter #(.max('hfff), .width(12)) counter_1 (
    .clr(or_1_out), .load(PI), .up(1'b1), .count(INC), .clk(CLK), .D(controlled_buffer_2_out[11:0]),
    .carry(counter_1_carry), .Q(counter_1_q));
endmodule
